// Logisim project PFC_v2.circ as structural Verilog: 1 circuit, main circuit main
module main (
);

  wire clock_1_out, clock_2_out, clock_3_out, clock_4_out;

  Register IF_ID (.clk(clock_1_out));  // open: D, en, Q, clr
  Clock clock_1 (.out(clock_1_out));
  ROM uCode ();  // open: addr, data
  Register ID_EX (.clk(clock_2_out));  // open: D, en, Q, clr
  Clock clock_2 (.out(clock_2_out));
  Register EX_MEM (.clk(clock_3_out));  // open: D, en, Q, clr
  Clock clock_3 (.out(clock_3_out));
  Register MEM_WB (.clk(clock_4_out));  // open: D, en, Q, clr
  Clock clock_4 (.out(clock_4_out));
endmodule
