// Logisim project PFC_mini.circ as structural Verilog: 4 circuits, main circuit main
module main (
  input  Start,
  input  Reset
);

  wire ADDR_A, ADDR_B, ADDR_C, ADDR_D, ADDR_Opnd, ALU_CF, ALU_En, ALU_NF, ALU_OF, ALU_ZF, and_1_out,
       and_2_out, and_3_out, and_5_out, and_6_out, and_7_out, and_8_out, and_9_out, and_10_out, and_11_out,
       clock_2_out, clock_3_out, clock_4_out, clock_6_out, clock_7_out, clock_8_out, clock_9_out,
       clock_10_out, clock_11_out, clock_12_out, clock_13_out, clock_14_out, clock_15_out, clock_16_out,
       clock_17_out, clock_18_out, decoder_1_out6, decoder_1_out7, Execute_1, Execute_2, Fetch_1, Fetch_2,
       Idle, In_0_En, In_1_En, In_2_En, In_3_En, Jump_En, MMIO, multiplexer_2_out, multiplexer_3_out,
       multiplexer_4_out, multiplexer_6_out, multiplexer_7_out, not_1_out, random_1_p2, S_CF, S_NF, S_OF,
       S_ZF, Set_PC, xor_1_out;
  wire [2:0] CPU_state;
  wire [3:0] bin_to_bcd_16_1_out_1, bin_to_bcd_16_1_out_10, bin_to_bcd_16_1_out_100,
       bin_to_bcd_16_1_out_1000, bin_to_bcd_16_1_out_10000, In_0;
  wire [7:0] A, Address, Address_bus, ALU_out, B, C, D, Data_bus, In_1, In_2, In_3, multiplexer_1_out,
       multiplexer_5_out, Opcode, Operand, PC, PC_plus_1, Program_out, register_1_q;
  wire [15:0] register_2_q;
  wire [23:0] Control_signals;

  Button button_1 (.out(In_0[3]));
  Button button_2 (.out(In_0[0]));
  Button button_3 (.out(In_0[2]));
  Button button_4 (.out(In_0[1]));
  // Random random_1: pin names not known; wires that end beside it: 1'b1, random_1_p2
  Clock clock_1 (.out(random_1_p2));
  Register register_1 (.D(Data_bus), .en(and_1_out), .clk(clock_2_out), .Q(register_1_q));  // open: clr
  and and_1 (and_1_out, Control_signals[5], In_0_En);
  Clock clock_2 (.out(clock_2_out));
  and and_2 (and_2_out, Control_signals[5], In_1_En);
  Hex_Digit_Display hex_digit_display_1 (.value(A[7:4]));  // open: dp
  Hex_Digit_Display hex_digit_display_2 (.value(A[3:0]));  // open: dp
  Hex_Digit_Display hex_digit_display_3 (.value(C[7:4]));  // open: dp
  Hex_Digit_Display hex_digit_display_4 (.value(C[3:0]));  // open: dp
  Hex_Digit_Display hex_digit_display_5 (.value(PC[7:4]));  // open: dp
  Hex_Digit_Display hex_digit_display_6 (.value(PC[3:0]));  // open: dp
  Clock clock_3 (.out(clock_3_out));
  Register #(.width(16)) register_2 (
    .D({Data_bus, register_1_q}), .en(and_2_out), .clk(clock_4_out), .Q(register_2_q));  // open: clr
  Clock clock_4 (.out(clock_4_out));
  Clock clock_5 ();  // open: out
  TTY tty_1 (.data(Data_bus[6:0]), .clk(clock_3_out), .we(and_3_out));  // open: clr
  and and_3 (and_3_out, In_0_En, Control_signals[5]);
  Hex_Digit_Display hex_digit_display_7 (.value(bin_to_bcd_16_1_out_10000));  // open: dp
  Hex_Digit_Display hex_digit_display_8 (.value(bin_to_bcd_16_1_out_1000));  // open: dp
  Hex_Digit_Display hex_digit_display_9 (.value(B[7:4]));  // open: dp
  Hex_Digit_Display hex_digit_display_10 (.value(B[3:0]));  // open: dp
  Hex_Digit_Display hex_digit_display_11 (.value(D[7:4]));  // open: dp
  Hex_Digit_Display hex_digit_display_12 (.value(D[3:0]));  // open: dp
  LED led_1 (.in(Idle));
  LED led_2 (.in(Fetch_1));
  LED led_3 (.in(Fetch_2));
  LED led_4 (.in(Execute_1));
  LED led_5 (.in(Execute_2));
  Hex_Digit_Display hex_digit_display_13 (.value(bin_to_bcd_16_1_out_100));  // open: dp
  Hex_Digit_Display hex_digit_display_14 (.value(bin_to_bcd_16_1_out_10));  // open: dp
  Bin_to_BCD_16 bin_to_bcd_16_1 (
    .Bin(register_2_q), .Out_1(bin_to_bcd_16_1_out_1), .Out_10(bin_to_bcd_16_1_out_10),
    .Out_100(bin_to_bcd_16_1_out_100), .Out_1000(bin_to_bcd_16_1_out_1000),
    .Out_10000(bin_to_bcd_16_1_out_10000));
  Hex_Digit_Display hex_digit_display_15 (.value(bin_to_bcd_16_1_out_1));  // open: dp
  Multiplexer #(.width(8)) multiplexer_1 (.in0(Data_bus), .in1(ALU_out), .out(multiplexer_1_out), .sel(ALU_En));
  Register u_A (.D(multiplexer_1_out), .en(Control_signals[1]), .clk(clock_6_out), .Q(A), .clr(Reset));
  Clock clock_6 (.out(clock_6_out));
  D_Flip_Flop Flag_ZF (.D(multiplexer_2_out), .clk(clock_7_out), .Q(S_ZF), .reset(Reset));  // open: Qn, preset
  Multiplexer multiplexer_2 (.in0(S_ZF), .in1(ALU_ZF), .out(multiplexer_2_out), .sel(ALU_En));
  Clock clock_7 (.out(clock_7_out));
  ROM Program_Memory (.addr(PC), .data(Program_out));
  and and_4 (MMIO, Address[2], Address[3], Address[4], Address[5], Address[6], Address[7]);
  Register MAR (.D(Address_bus), .en(Execute_1), .clk(clock_8_out), .Q(Address), .clr(Reset));
  Clock clock_8 (.out(clock_8_out));
  Control_Unit control_unit_1 (
    .Start(Start), .Program_out(Program_out), .Opcode(Opcode), .Reset(Reset), .CPU_state(CPU_state),
    .Control_signals({Control_signals[23:18], ALU_En, ADDR_Opnd, ADDR_D, ADDR_C, ADDR_B, ADDR_A, Control_signals[11:0]}));
  Clock clock_9 (.out(clock_9_out));
  Register u_B (.D(Data_bus), .en(Control_signals[2]), .clk(clock_10_out), .Q(B), .clr(Reset));
  Clock clock_10 (.out(clock_10_out));
  D_Flip_Flop Flag_NF (.D(multiplexer_3_out), .clk(clock_9_out), .Q(S_NF), .reset(Reset));  // open: Qn, preset
  Multiplexer multiplexer_3 (.in0(S_NF), .in1(ALU_NF), .out(multiplexer_3_out), .sel(ALU_En));
  Clock clock_11 (.out(clock_11_out));
  Decoder #(.enable("false"), .select(3)) decoder_1 (
    .out0(Idle), .out1(Fetch_1), .out4(Execute_2), .out5(Execute_1), .out6(decoder_1_out6),
    .out7(decoder_1_out7), .sel(CPU_state));  // open: out2, out3
  RAM #(.databus("bidir"), .enables("line"), .trigger("high")) Data_Memory (
    .addr(Address), .we(and_5_out), .oe(and_6_out), .clk(not_1_out), .data(Data_bus));
  and and_5 (and_5_out, Control_signals[5], not_1_out, clock_11_out);
  and and_6 (and_6_out, Control_signals[10], not_1_out);
  not not_1 (not_1_out, MMIO);
  or or_1 (Fetch_2, decoder_1_out6, decoder_1_out7);
  Register u_C (.D(Data_bus), .en(Control_signals[3]), .clk(clock_12_out), .Q(C), .clr(Reset));
  Clock clock_12 (.out(clock_12_out));
  D_Flip_Flop Flag_CF (.D(multiplexer_4_out), .clk(clock_13_out), .Q(S_CF), .reset(Reset));  // open: Qn, preset
  Multiplexer multiplexer_4 (.in0(S_CF), .in1(ALU_CF), .out(multiplexer_4_out), .sel(Control_signals[18]));
  Clock clock_13 (.out(clock_13_out));
  Multiplexer #(.width(8)) multiplexer_5 (.in0(PC_plus_1), .in1(Operand), .out(multiplexer_5_out), .sel(Jump_En));
  or or_2 (Set_PC, Fetch_1, Fetch_2, Jump_En);
  Multiplexer #(.select(2)) multiplexer_6 (
    .in0(S_ZF), .in1(S_NF), .in2(S_CF), .in3(S_OF), .out(multiplexer_6_out), .sel(Opcode[1:0]));
  xor xor_1 (xor_1_out, multiplexer_6_out, Opcode[2]);
  Register u_D (.D(Data_bus), .en(Control_signals[4]), .clk(clock_14_out), .Q(D), .clr(Reset));
  Clock clock_14 (.out(clock_14_out));
  D_Flip_Flop Flag_OF (.D(multiplexer_7_out), .clk(clock_15_out), .Q(S_OF), .reset(Reset));  // open: Qn, preset
  Multiplexer multiplexer_7 (.in0(S_OF), .in1(ALU_OF), .out(multiplexer_7_out), .sel(Control_signals[19]));
  Clock clock_15 (.out(clock_15_out));
  Register u_PC (.D(multiplexer_5_out), .en(Set_PC), .clk(clock_16_out), .Q(PC), .clr(Reset));
  Clock clock_16 (.out(clock_16_out));
  and and_7 (and_7_out, Control_signals[21], xor_1_out);
  Adder adder_1 (.a(PC), .b(8'h1), .out(PC_plus_1), .cin(1'b0));  // open: cout
  or or_3 (Jump_En, Control_signals[20], and_7_out);
  Decoder #(.select(2)) decoder_2 (
    .out0(In_0_En), .out1(In_1_En), .out2(In_2_En), .out3(In_3_En), .sel(Address[1:0]), .en(MMIO));
  assign Data_bus = Control_signals[6] ? A : 8'bz;  // Controlled_Buffer controlled_buffer_1
  assign Data_bus = Control_signals[7] ? B : 8'bz;  // Controlled_Buffer controlled_buffer_2
  assign Data_bus = Control_signals[8] ? C : 8'bz;  // Controlled_Buffer controlled_buffer_3
  assign Data_bus = Control_signals[9] ? D : 8'bz;  // Controlled_Buffer controlled_buffer_4
  assign Data_bus = Control_signals[11] ? Operand : 8'bz;  // Controlled_Buffer controlled_buffer_5
  Pull_Resistor pull_resistor_1 (.node(Data_bus));
  Register u_Opcode (.D(Program_out), .en(Fetch_1), .clk(clock_17_out), .Q(Opcode), .clr(Reset));
  Clock clock_17 (.out(clock_17_out));
  Register u_Operand (.D(Program_out), .en(Fetch_2), .clk(clock_18_out), .Q(Operand), .clr(Reset));
  Clock clock_18 (.out(clock_18_out));
  and and_8 (and_8_out, Control_signals[10], In_0_En);
  and and_9 (and_9_out, Control_signals[10], In_1_En);
  and and_10 (and_10_out, Control_signals[10], In_2_En);
  and and_11 (and_11_out, Control_signals[10], In_3_En);
  assign Data_bus = and_8_out ? {4'b0000, In_0} : 8'bz;  // Controlled_Buffer controlled_buffer_6
  assign Data_bus = and_9_out ? In_1 : 8'bz;  // Controlled_Buffer controlled_buffer_7
  assign Data_bus = and_10_out ? In_2 : 8'bz;  // Controlled_Buffer controlled_buffer_8
  assign Data_bus = and_11_out ? In_3 : 8'bz;  // Controlled_Buffer controlled_buffer_9
  assign Address_bus = ADDR_A ? A : 8'bz;  // Controlled_Buffer controlled_buffer_10
  assign Address_bus = ADDR_B ? B : 8'bz;  // Controlled_Buffer controlled_buffer_11
  assign Address_bus = ADDR_C ? C : 8'bz;  // Controlled_Buffer controlled_buffer_12
  assign Address_bus = ADDR_D ? D : 8'bz;  // Controlled_Buffer controlled_buffer_13
  assign Address_bus = ADDR_Opnd ? Operand : 8'bz;  // Controlled_Buffer controlled_buffer_14
  ALU alu_1 (
    .Opcode(Opcode), .A(A), .B(Data_bus), .CF_in(S_CF), .Result(ALU_out), .ZF_out(ALU_ZF), .NF_out(ALU_NF),
    .CF_out(ALU_CF), .OF_out(ALU_OF));
  Pull_Resistor pull_resistor_2 (.node(Address_bus));

  // Other names for the same wires on the sheet: WR_A = Control_signals[1]; WR_B = Control_signals[2];
  //   WR_C = Control_signals[3]; WR_D = Control_signals[4]; WR_RAM = Control_signals[5]; RD_A = Control_signals[6];
  //   RD_B = Control_signals[7]; RD_C = Control_signals[8]; RD_D = Control_signals[9]; RD_RAM = Control_signals[10];
  //   RD_Opnd = Control_signals[11]; Control_signals[17:12] = {ALU_En, ADDR_Opnd, ADDR_D, ADDR_C, ADDR_B, ADDR_A};
  //   Set_CF = Control_signals[18]; Set_OF = Control_signals[19]; JMP = Control_signals[20];
  //   JMP_Cond = Control_signals[21]; Halt = Control_signals[22]

  // Notes on the sheet:
  //   contents of Program_Memory (hex, n*v repeats v):
  //   a8 50 0 50 1 50 3 10 1 50 2 70 0 74 2 81 54 0 50 2 8 70 1 74 3 89 54 1 50 3 3a 26 58 fc 50 fd 30 b
  //   28
endmodule

module Control_Unit (
  input  Start,
  input  [7:0] Program_out,
  input  [7:0] Opcode,
  input  Reset,
  output [2:0] CPU_state,
  output [23:0] Control_signals
);

  wire clock_1_out, decoder_1_out6, decoder_1_out7, Execute_1, Execute_2, Fetch_1, Fetch_2, HALT, Idle,
       Length_2, WR_MAR;
  wire [2:0] CPU_next_state;
  wire [3:2] undriven, undriven_2;
  wire [4:0] bit_extender_2_out;
  wire [4:2] undriven_3;
  wire [7:0] multiplexer_4_out, uCode_ROM_2_data, uCode_ROM_3_data;
  wire [7:1] uCode_ROM_1_data;
  wire [18:0] bit_extender_1_out;

  not not_1 (undriven_3[4], HALT);
  Register #(.width(3)) CPU_state_reg (.D(CPU_next_state), .en(1'b1), .clk(clock_1_out), .Q(CPU_state), .clr(Reset));
  Clock clock_1 (.out(clock_1_out));
  Multiplexer #(.select(3)) multiplexer_1 (
    .in0(1'b0), .in1(1'b1), .in2(undriven[2]), .in3(undriven[3]), .in4(1'b0), .in5(1'b1), .in6(1'b1),
    .in7(1'b1), .out(CPU_next_state[2]), .sel(CPU_state));
  Multiplexer #(.select(3)) multiplexer_2 (
    .in0(1'b0), .in1(Length_2), .in2(undriven_2[2]), .in3(undriven_2[3]), .in4(1'b0), .in5(1'b0), .in6(1'b0),
    .in7(1'b0), .out(CPU_next_state[1]), .sel(CPU_state));
  Multiplexer #(.select(3)) multiplexer_3 (
    .in0(Start), .in1(WR_MAR), .in2(undriven_3[2]), .in3(undriven_3[3]), .in4(undriven_3[4]), .in5(1'b0),
    .in6(WR_MAR), .in7(WR_MAR), .out(CPU_next_state[0]), .sel(CPU_state));
  Decoder #(.enable("false"), .select(3)) decoder_1 (
    .out0(Idle), .out1(Fetch_1), .out4(Execute_2), .out5(Execute_1), .out6(decoder_1_out6),
    .out7(decoder_1_out7), .sel(CPU_state));  // open: out2, out3
  Multiplexer #(.width(8)) multiplexer_4 (.in0(Opcode), .in1(Program_out), .out(multiplexer_4_out), .sel(Fetch_1));
  or or_1 (Fetch_2, decoder_1_out6, decoder_1_out7);
  ROM uCode_ROM_1 (.addr(multiplexer_4_out), .data({uCode_ROM_1_data, Length_2}));
  ROM uCode_ROM_2 (.addr(multiplexer_4_out), .data(uCode_ROM_2_data));
  ROM uCode_ROM_3 (.addr(multiplexer_4_out), .data({uCode_ROM_3_data[7], HALT, uCode_ROM_3_data[5:0]}));
  or or_2 (WR_MAR, uCode_ROM_1_data[5], uCode_ROM_2_data[2]);
  assign bit_extender_1_out = {{18{Execute_2}}, Execute_2};  // Bit_Extender bit_extender_1
  assign bit_extender_2_out = {{4{Execute_1}}, Execute_1};  // Bit_Extender bit_extender_2
  assign {Control_signals[23:17], Control_signals[11:0]} = bit_extender_1_out & {uCode_ROM_3_data[7], HALT, uCode_ROM_3_data[5:1], uCode_ROM_2_data[3:0], uCode_ROM_1_data, Length_2};  // AND_Gate and_1, 19 bits wide
  assign Control_signals[16:12] = bit_extender_2_out & {uCode_ROM_3_data[0], uCode_ROM_2_data[7:4]};  // AND_Gate and_2, 5 bits wide

  // Notes on the sheet:
  //   contents of uCode_ROM_1 (hex, n*v repeats v):
  //   42 82 2 2 44 84 4 4 48 88 8 8 50 90 10 10 4*3 4*5 4*9 4*11 16*0 16*1 4*60 4*a0 8*20 4*61 4*a1 8*21
  //   4*2 4*4 4*8 4*10 4*3 4*5 4*9 4*11 42 82 2 2 42 82 2 2 42 82 2 2 42 82 2 2 16*3 42 82 2 2 42 82 2 2
  //   42 82 6*2 12*3 4*2 4*0 40 80 14*0 4*1 8*0 40 80 14*0 4*1
  //   contents of uCode_ROM_2 (hex, n*v repeats v):
  //   0 0 1 2 0 0 1 2 0 0 1 2 0 0 1 2 16*8 32*0 10 20 40 80 10 20 40 80 11 21 41 81 12 22 42 82 8*0 4*1
  //   4*2 14 24 44 84 14 24 44 84 14 24 44 84 14 24 44 84 16*4 0 0 1 2 0 0 1 2 0 0 1 2 0 0 1 2 16*8 0 0 1
  //   2 0 0 1 2 0 0 1 2 4*0 12*8 10*0 1 2 12*0 4*8 10*0 1 2 12*0 4*8
  //   contents of uCode_ROM_3 (hex, n*v repeats v):
  //   40*0 8*40 8*10 8*20 16*0 16*1 16*0 16*1 32*e 12*2 4*6 12*2 4*6 4*0 4*e 12*0 4*e 8*0 4*2 12*0 4*2
endmodule

module ALU (
  input  [7:0] Opcode,
  input  [7:0] A,
  input  [7:0] B,
  input  CF_in,
  output [7:0] Result,
  output ZF_out,
  output NF_out,
  output CF_out,
  output OF_out
);

  wire Adder_Cin, Adder_Cout, ALU_ADC, ALU_ADD, ALU_AND, ALU_OR, ALU_ROR, ALU_SBC, ALU_SHR, ALU_SHR_ROR,
       ALU_SUB, ALU_subtract, ALU_XOR, and_1_out, and_6_out, and_7_out, and_8_out, and_9_out, and_10_out,
       and_11_out, not_1_out, not_2_out, not_3_out, not_4_out, not_5_out, not_6_out, or_1_out, ROR_Cin;
  wire [7:0] adder_1_out, and_5_out, bit_extender_1_out, multiplexer_1_out, or_4_out, xor_1_out, xor_2_out;

  or or_1 (or_1_out, ALU_ADC, ALU_SBC);
  Decoder #(.enable("false"), .select(3)) decoder_1 (
    .out0(ALU_ADD), .out1(ALU_SUB), .out2(ALU_ADC), .out3(ALU_SBC), .out4(ALU_AND), .out5(ALU_OR),
    .out6(ALU_XOR), .out7(ALU_SHR_ROR), .sel({Opcode[5], Opcode[3:2]}));
  or or_2 (ALU_subtract, ALU_SUB, ALU_SBC);
  or or_3 (Adder_Cin, ALU_SUB, and_1_out);
  and and_1 (and_1_out, or_1_out, CF_in);
  and and_2 (ALU_SHR, ALU_SHR_ROR, not_1_out);
  not not_1 (not_1_out, Opcode[5]);
  and and_3 (ALU_ROR, ALU_SHR_ROR, Opcode[5]);
  and and_4 (ROR_Cin, CF_in, ALU_ROR);
  assign bit_extender_1_out = {{7{ALU_subtract}}, ALU_subtract};  // Bit_Extender bit_extender_1
  assign xor_1_out = B ^ bit_extender_1_out;  // XOR_Gate xor_1, 8 bits wide
  assign and_5_out = A & B;  // AND_Gate and_5, 8 bits wide
  assign or_4_out = A | B;  // OR_Gate or_4, 8 bits wide
  assign xor_2_out = A ^ B;  // XOR_Gate xor_2, 8 bits wide
  Adder adder_1 (.a(A), .b(xor_1_out), .out(adder_1_out), .cin(Adder_Cin), .cout(Adder_Cout));
  Multiplexer #(.select(2), .width(8)) multiplexer_1 (
    .in0(and_5_out), .in1(or_4_out), .in2(xor_2_out), .in3({ROR_Cin, A[7:1]}), .out(multiplexer_1_out),
    .sel(Opcode[3:2]));
  Multiplexer #(.width(8)) multiplexer_2 (
    .in0(adder_1_out), .in1(multiplexer_1_out), .out({NF_out, Result[6:0]}), .sel(Opcode[4]));
  not not_2 (not_2_out, A[7]);
  not not_3 (not_3_out, B[7]);
  not not_4 (not_4_out, NF_out);
  not not_5 (not_5_out, Opcode[2]);
  and and_6 (and_6_out, A[0], ALU_SHR_ROR);
  and and_7 (and_7_out, Adder_Cout, not_6_out);
  not not_6 (not_6_out, Opcode[4]);
  and and_8 (and_8_out, not_2_out, not_3_out, NF_out, not_5_out);
  and and_9 (and_9_out, A[7], B[7], not_4_out, not_5_out);
  and and_10 (and_10_out, not_2_out, B[7], NF_out, Opcode[2]);
  and and_11 (and_11_out, A[7], not_3_out, not_4_out, Opcode[2]);
  nor nor_1 (ZF_out, Result[0], Result[1], Result[2], Result[3], Result[4], Result[5], Result[6], NF_out);
  or or_5 (CF_out, and_6_out, and_7_out);
  or or_6 (OF_out, and_8_out, and_9_out, and_10_out, and_11_out);

  assign Result[7] = NF_out;

  // Other names for the same wires on the sheet: ALU_A[7:0] = A; SHR_Cout = A[0]; ALU_B[7:0] = B; ALU_CF = CF_out;
  //   ALU_OF = OF_out; ALU_out[7:0] = {NF_out, Result[6:0]}; ALU_NF = NF_out; ALU_ZF = ZF_out; S_CF = CF_in
endmodule

module Bin_to_BCD_16 (
  input  [15:0] Bin,
  output [3:0] Out_1,
  output [3:0] Out_10,
  output [3:0] Out_100,
  output [3:0] Out_1000,
  output [3:0] Out_10000
);

  wire [15:0] divider_1_out, divider_2_out, divider_3_out, divider_4_out;
  wire [15:4] divider_1_rem, divider_2_rem, divider_3_rem, divider_4_rem, divider_5_rem;

  Divider #(.width(16)) divider_1 (
    .a(Bin), .b(16'ha), .out(divider_1_out), .rem({divider_1_rem, Out_1}));  // open: upper
  Divider #(.width(16)) divider_2 (
    .a(divider_1_out), .b(16'ha), .out(divider_2_out), .rem({divider_2_rem, Out_10}));  // open: upper
  Divider #(.width(16)) divider_3 (
    .a(divider_2_out), .b(16'ha), .out(divider_3_out), .rem({divider_3_rem, Out_100}));  // open: upper
  Divider #(.width(16)) divider_4 (
    .a(divider_3_out), .b(16'ha), .out(divider_4_out), .rem({divider_4_rem, Out_1000}));  // open: upper
  Divider #(.width(16)) divider_5 (.a(divider_4_out), .b(16'ha), .rem({divider_5_rem, Out_10000}));  // open: out, upper
endmodule
